# Fritzing sketch jukebox (saved by Fritzing 0.9.3b)

parts:
  DFRobot_DFPlayer_Mini1 = DFRobot DFPlayer Mini [part_number=DFR0299]
  LED1 = LED - 5mm [color="Red (633nm)" package="5 mm [THT]"]
  S1 = Round Pushbutton
  Part1 = Adafruit PN532 NFC RFID Controller Shield [part_number="Adafruit #789"]
  R2 = Resistor [tolerance=±5% resistance=220 package="0805 [SMD]"]
  R3 = Resistor [tolerance=±5% resistance=10k package="0402 [SMD]"]
  R1 = Resistor [tolerance=±5% resistance=1k package="0402 [SMD]"]
  SPKR1 = Loudspeaker  # not connected

nets:
  N1: DFRobot_DFPlayer_Mini1.VCC, Part1.5.0V
  N2: DFRobot_DFPlayer_Mini1.RX, Part1.N$107, R1.Pin_0
  N3: DFRobot_DFPlayer_Mini1.TX, Part1.D10
  N4: DFRobot_DFPlayer_Mini1.GND-1, Part1.N$70
  N5: LED1.cathode, Part1.GND, Part1.N$65
  N6: S1.leg1, Part1.+3.3V
  N7: Part1.D11, R1.Pin_1
  N8: Part1.D7, R2.Pin_1
  N9: Part1.D5, Part1.N$96
  N10: Part1.N$66, Part1.N$99, R3.Pin_1

custom parts:
  Adafruit PN532 NFC RFID Controller Shield: We've taken our popular Adafruit PN532 breakout board and turned it into a shield - the perfect tool for any 13.56MHz RFID or NFC application. The Adafruit NFC shield uses the PN532 chip-set (the most popular NFC chip on the market) and is what is embedded in pretty much every phone or device that does NFC. This chipset is very powerful, and can pretty much do it all, such as read and write to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
